# Fritzing sketch circuit (saved by Fritzing 1.0.1rc)
breadboards: 1

parts:
  Mod1 = Heltec WiFi LoRa 32 V2 [part_number=HTIT-WB32LA]
  J1 = Piezo Speaker
  J2 = Piezo Speaker
  S1 = Round Pushbutton
  S2 = Round Pushbutton
  S3 = Round Pushbutton
  S4 = Round Pushbutton
  HC-SR04_Sensor_1 = HC-SR04 Ultrasonic Distance Sensor

nets:
  N1: Mod1.pin_16, Mod1.pin_17
  GND: Mod1.GND, J1.pin1, J2.pin1, S1.leg0, S2.leg0, S3.leg0, S4.leg0, HC-SR04_Sensor_1.GND
  N2: Mod1.pin_20, HC-SR04_Sensor_1.VCC
  N3: Mod1.pin_21, Mod1.pin_22
  N4: Mod1.pin_27, HC-SR04_Sensor_1.ECHO
  N5: Mod1.pin_28, J2.pin2
  N6: Mod1.pin_29, HC-SR04_Sensor_1.TRIG
  N7: Mod1.pin_30, S1.leg1
  N8: Mod1.pin_31, J1.pin2
  N9: Mod1.pin_32, S4.leg1
  N10: Mod1.pin_35, S2.leg1
  N11: Mod1.pin_36, S3.leg1
